# Fritzing sketch DCC_Turnout_Decoder_direct (saved by Fritzing 0.9.3b)
circuit board: 8.5cm x 10cm
breadboards: 1

parts:
  Nano = Arduino Nano (Rev3.0)
  -2 = female pin header, 2 pins [form="♀ (female)"]
  BR3 = female alternating pin header, 2 pins [form="♀ (female)"]
  C2 = Electrolytic Capacitor [capacitance=22µF voltage=20V package="100 mil [THT, electrolytic]"]
  C1 = Tantalum Capacitor [capacitance=1µF voltage=20V package="100 mil [THT, tantalum]"]
  C3 = Tantalum Capacitor [capacitance=1µF voltage=20V package="100 mil [THT, tantalum]"]
  IC2 = IC, DIP package, 8 pins [chip_label=IC]
  R1 = Resistor [tolerance=±5% resistance=1k power=0.25 package=THT]
  D1 = Rectifier Diode [part_number=1N4001 package="300 mil [THT]"]
  C4 = Ceramic Capacitor [capacitance=100nF package="100 mil [THT, multilayer]"]
  R2 = Resistor [tolerance=±5% resistance=10k power=0.25 package=THT]
  R3 = Resistor [tolerance=±5% resistance=10k power=0.25 package=THT]
  U1 = Voltage Regulator - 5V [package="TO220 [THT]"]
  J18 = screw terminal, 2 pins
  J19 = female pin header, 2 pins [form="♀ (female)"]
  D3 = Zener Diode [part_number=1N4749A breakdown_voltage=24V package="300 mil [THT]"]
  J20 = female pin header, 1 pin [form="♀ (female)"]
  J21 = screw terminal, 2 pins
  -3 = female pin header, 2 pins [form="♀ (female)"]
  BR4 = female alternating pin header, 2 pins [form="♀ (female)"]
  R8 = Resistor [tolerance=±5% resistance=2.2k power=0.25 package=THT]
  R9 = Resistor [tolerance=±5% resistance=2.2k power=0.25 package=THT]
  R10 = Resistor [tolerance=±5% resistance=2.2k power=0.25 package=THT]
  Q3 = npn-Powertransistor [part_number=TIP41C package="TO220 [THT]"]
  C5 = Electrolytic Capacitor [capacitance=410µ voltage=35V part_number=10000µF package="300 mil [THT, electrolytic]"]
  D4 = Rectifier Diode [part_number=1N4007 package="300 mil [THT]"]
  1 = female pin header, 3 pins [form="♀ (female)"]
  2 = female pin header, 3 pins [form="♀ (female)"]
  3 = female pin header, 3 pins [form="♀ (female)"]
  4 = female pin header, 3 pins [form="♀ (female)"]
  5 = female pin header, 3 pins [form="♀ (female)"]
  6 = female pin header, 3 pins [form="♀ (female)"]
  7 = female pin header, 3 pins [form="♀ (female)"]
  8 = female pin header, 3 pins [form="♀ (female)"]
  ULN3 = Darlington Driver [package=dil18]
  ULN4 = Darlington Driver [package=dil18]
  LED1 = LED - 3mm [color="Blue (505nm)" current=0.030 package="3 mm [THT]"]
  R11 = Resistor [tolerance=±5% power=0.25 resistance=2.2k package=THT]
  J22 = female pin header, 1 pin [form="♀ (female)"]
  J23 = female pin header, 1 pin [form="♀ (female)"]
  J24 = female pin header, 1 pin [form="♀ (female)"]
  J25 = female pin header, 1 pin [form="♀ (female)"]
  J26 = female pin header, 2 pins [form="♀ (female)"]
  R12 = Resistor [tolerance=±5% power=0.25 resistance=10k package=THT]
  Learn = female pin header, 2 pins [form="♀ (female)"]

nets:
  GND: Nano.GND, -2.pin1, C2.-, C1.-, C3.-, IC2.pin5, U1.GND, J19.pin1, J19.pin2, D3.anode, -3.pin1, C5.-, ULN3.9, ULN4.9, R11.Pin_0, J24.pin1, J25.pin1, R12.Pin_0
  N1: Nano.D2, IC2.pin6, R2.Pin_0
  N2: Nano.D3, ULN3.8
  N3: Nano.D4, ULN3.7
  N4: Nano.D5, ULN3.6
  N5: Nano.D6, ULN3.5
  N6: Nano.D7, ULN3.4
  N7: Nano.D8, ULN3.3
  N8: Nano.D9, ULN3.2
  N9: Nano.D10, ULN3.1
  N10: Nano.D11/MOSI, ULN4.8
  N11: Nano.D12/MISO, ULN4.7
  N12: Nano.5V, C2.+, C3.+, IC2.pin8, R2.Pin_1, R3.Pin_1, U1.output_voltage, Learn.pin1
  N13: Nano.A6, R12.Pin_1, Learn.pin2
  N14: Nano.A5, ULN4.1
  N15: Nano.A4, ULN4.2
  N16: Nano.A3, ULN4.3
  N17: Nano.A2, ULN4.4
  N18: Nano.A0, ULN4.5
  N19: Nano.D13/SCK, ULN4.6
  N20: -2.pin2, IC2.pin3, D1.anode, C4.1, J18.pin2
  N21: BR3.pin1, R1.Pin_0, J18.pin1
  N22: BR3.pin2, C1.+, U1.input_voltage
  N23: IC2.pin2, R1.Pin_1, D1.cathode, C4.0
  N24: IC2.pin7, R3.Pin_0
  N25: D3.cathode, J20.pin1, Q3.emitter, C5.+, D4.anode
  N26: J21.pin1, BR4.pin1
  N27: J21.pin2, -3.pin2
  N28: BR4.pin2, R8.Pin_1, R9.Pin_1, R10.Pin_1, J22.pin1, J26.pin2
  N29: R8.Pin_0, R9.Pin_0, R10.Pin_0, Q3.base
  N30: Q3.collector, J23.pin1, J26.pin1
  N31: D4.cathode, 1.pin1, 2.pin1, 3.pin1, 4.pin1, 5.pin1, 6.pin1, 7.pin1, 8.pin1, ULN3.10, ULN4.10, LED1.anode
  N32: 1.pin2, ULN3.12
  N33: 1.pin3, ULN3.11
  N34: 2.pin2, ULN3.14
  N35: 2.pin3, ULN3.13
  N36: 3.pin2, ULN3.16
  N37: 3.pin3, ULN3.15
  N38: 4.pin2, ULN3.18
  N39: 4.pin3, ULN3.17
  N40: 5.pin2, ULN4.12
  N41: 5.pin3, ULN4.11
  N42: 6.pin2, ULN4.14
  N43: 6.pin3, ULN4.13
  N44: 7.pin2, ULN4.16
  N45: 7.pin3, ULN4.15
  N46: 8.pin2, ULN4.18
  N47: 8.pin3, ULN4.17
  N48: LED1.cathode, R11.Pin_1

notes:
  1
  RT DCC TD8 2
  +
  DCC In
  B
  C
  T
  Input
  Base turnout address
